# Fritzing sketch CorsairController (saved by Fritzing 0.9.3b)
stripboards: 2

parts:
  Master = Pro Micro
  ARGB1 = female pin header, 3 pins [form="♀ (female)"]
  ARGB2 = female pin header, 3 pins [form="♀ (female)"]
  RGB = female pin header, 4 pins [form="♀ (female)"]
  R = Basic FET N-Channel [package="TO220 [THT]"]
  G = Basic FET N-Channel [package="TO220 [THT]"]
  B = Basic FET N-Channel [package="TO220 [THT]"]
  FAN1 = Basic FET N-Channel [package="TO220 [THT]"]
  FAN1_2 = female pin header, 3 pins [form="♀ (female)"]
  FAN2 = Basic FET N-Channel [package="TO220 [THT]"]
  FAN2_2 = female pin header, 3 pins [form="♀ (female)"]
  Slave = Pro Micro
  FAN3 = Basic FET N-Channel [package="TO220 [THT]"]
  UART = female pin header, 5 pins [form="♀ (female)"]
  UART_2 = male pin header, 5 pins [form="♂ (male)"]
  FAN3_2 = female pin header, 3 pins [form="♀ (female)"]
  FAN4 = Basic FET N-Channel [package="TO220 [THT]"]
  FAN4_2 = female pin header, 3 pins [form="♀ (female)"]
  FAN5 = female pin header, 3 pins [form="♀ (female)"]
  FAN5_2 = Basic FET N-Channel [package="TO220 [THT]"]
  FAN6 = female pin header, 3 pins [form="♀ (female)"]
  FAN6_2 = Basic FET N-Channel [package="TO220 [THT]"]
  Power = female pin header, 3 pins [form="♀ (female)"]

nets:
  N1: Master.TX1, UART.pin4
  N2: Master.RX0, UART.pin3
  N3: Master.D3, FAN2.gate
  N4: Master.D5, FAN1.gate
  N5: Master.D6, R.gate
  N6: Master.D7, ARGB1.pin2
  N7: Master.D8, ARGB2.pin2
  N8: Master.D9, G.gate
  N9: Master.D10, B.gate
  GND: Master.GND, ARGB1.pin1, ARGB2.pin1, RGB.pin1, R.source, G.source, B.source, FAN1.source, FAN2.source, UART.pin5, Power.pin3
  12V: Master.RAW, ARGB1.pin3, ARGB2.pin3, FAN1_2.pin2, FAN2_2.pin2, UART.pin1, Power.pin1
  N10: RGB.pin2, R.drain
  N11: RGB.pin3, G.drain
  N12: RGB.pin4, B.drain
  N13: FAN1.drain, FAN1_2.pin3
  N14: FAN2.drain, FAN2_2.pin3
  N15: Slave.TX1, UART_2.pin3
  N16: Slave.RX0, UART_2.pin4
  N17: Slave.GND, FAN3.source, UART_2.pin5, FAN4.source, FAN5_2.source, FAN6_2.source
  N18: Slave.D3, FAN3.gate
  N19: Slave.D5, FAN4.gate
  N20: Slave.D6, FAN5_2.gate
  N21: Slave.D9, FAN6_2.gate
  N22: Slave.VCC, UART_2.pin2
  N23: FAN3.drain, FAN3_2.pin3
  5V: UART.pin2, Power.pin2
  N24: UART_2.pin1, FAN3_2.pin2, FAN4_2.pin2, FAN5.pin2, FAN6.pin2
  N25: FAN4.drain, FAN4_2.pin3
  N26: FAN5.pin3, FAN5_2.drain
  N27: FAN6.pin3, FAN6_2.drain

custom parts:
  Pro Micro: The SparkFun Pro Micro is a complete USB-based microcontoller development system, in a very small footprint, capable of implementing many types of projects. All programming can be done via the USB port.
